# Fritzing sketch Nano Motivator v1 (saved by Fritzing 1.0.5)
breadboards: 1

parts:
  C1 = Capacitor Polarized [package=cpol-radial-10uf-25v]
  Part2 = Adafruit Breadboard-Friendly NeoPixel [part_number="Adafruit #1312"]
  Part3 = Adafruit Breadboard-Friendly NeoPixel [part_number="Adafruit #1312"]
  U1 = 74AHCT125 [part_number=SN74AHCT125 package=dil14]
  A1 = Arduino Nano ESP32
  DFRobot_DFPlayer_Mini2 = DFRobot DFPlayer Mini [part_number=DFR0299]
  J2 = Piezo Speaker
  SP3 = SPEAKER [package=pcb_mount_speaker]
  SP4 = SPEAKER [package=pcb_mount_speaker]

nets:
  N1: C1.+, A1.Pin_15, DFRobot_DFPlayer_Mini2.VCC
  N2: C1.-, A1.Pin_14, A1.Pin_19, DFRobot_DFPlayer_Mini2.GND-1, DFRobot_DFPlayer_Mini2.GND-2, SP3.+, SP4.+
  N3: Part2.IN, U1.1OE
  N4: Part3.IN, U1.1A
  N5: U1.4OE, A1.Pin_25
  N6: U1.VCC, A1.Pin_24
  N7: A1.Pin_20, DFRobot_DFPlayer_Mini2.TX
  N8: A1.Pin_21, DFRobot_DFPlayer_Mini2.RX
  N9: A1.Pin_22, DFRobot_DFPlayer_Mini2.BUSY
  N10: DFRobot_DFPlayer_Mini2.DAC_R, SP4.-
  N11: DFRobot_DFPlayer_Mini2.DAC_L, SP3.-
  N12: DFRobot_DFPlayer_Mini2.SPK_1, J2.pin2
  N13: DFRobot_DFPlayer_Mini2.SPK_2, J2.pin1

notes:
  74AHCT125 other 3.3-5v Level Shifter
  D9 SBUS IN (UART Rx1)
  From FrSky receiver
  100µF electrolytic capacitor - VCC-GND to steady DFPlayer power
  Longer lead to VCC
  DAC is for unamplified output (AMP not shown here) or phono pin
  Amplified 3W mono speaker - NO GND
  Yellow: DF Rx to D3 (Tx Software Serial 9600 Baud)
  Green: DF Tx to D2 (Rx Software Serial 9600 Baud)
  Blue: Busy to D4
  WS2812b LEDs Data only shown
  D6 LED BANK (1)
  D7 LED BANK (2)

custom parts:
  Adafruit Breadboard-Friendly NeoPixel: This is the easiest way possible to add small, bright RGB pixels to your project. We took the same technology from our Flora NeoPixels and made them breadboard friendly, with two rows of 3 x 0.1" spaced header on each side for easy soldering, chaining and breadboarding. These ultra-bright LEDs have a constant-current driver cooked right into the LED package! The pixels are chainable - so you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
  74AHCT125: Quad Level-Shifter (3V to 5V) Quadruple Bus Buffer Gates With 3-State Outputs
  Arduino Nano ESP32: Arduino® Nano ESP32 tht.
